# Fritzing sketch audio_vario (saved by Fritzing 0.9.3b)
breadboards: 1

parts:
  Part1 = Arduino Nano (Rev3.0)
  Part2 = Barometric Pressure Sensor - BMP180 Breakout (GY-68)
  Part5 = I2C level shifter bidirectional
  Mod1 = Passive Buzzer
  R1 = Resistor [tolerance=±5% power=0.25 resistance=10k package=THT]
  R2 = Resistor [tolerance=±5% power=0.25 resistance=10k package=THT]
  S1 = Pushbutton [package="[THT]"]
  S2 = Pushbutton [package="[THT]"]
  Part6 = Bluetooth module [part_number=101240]
  Part7 = I2C level shifter bidirectional
  R4 = Resistor [tolerance=±5% power=0.25 resistance=4.7k package=THT]
  R5 = Resistor [tolerance=±5% power=0.25 resistance=4.7k package=THT]
  Part8 = NCP1400 Step-Up Breakout
  U3 = POT_SWITCH [package=pot_pth_switch]
  VCC1 = Battery

nets:
  N1: Part1.D1/TX, Part7.HV2
  N2: Part1.D0/RX, Part7.HV1
  N3: Part1.D3, U3.G$2_2
  N4: Part1.D4, R2.Pin_1
  N5: Part1.D5, R1.Pin_1
  GND: Part1.GND, Part2.GND, Part5.GND, Mod1.-, R1.Pin_0, R2.Pin_0, S1.Pin_3, S1.Pin_4, S2.Pin_3, S2.Pin_4, Part6.GND, Part8.GND, VCC1.-
  5V: Part1.5V, Part5.HV3, S1.Pin_1, S1.Pin_2, S2.Pin_1, S2.Pin_2, Part6.VCC, R4.Pin_0, R5.Pin_0, Part8.VOUT
  N6: Part1.A5, Part5.HV, R4.Pin_1
  N7: Part1.A4, Part5.HV2, R5.Pin_1
  N8: Part2.VCC, Part5.LV3
  N9: Part2.SCL, Part5.LV
  N10: Part2.SDA, Part5.LV2
  N11: Mod1.S, U3.G$2_1
  N12: Part6.TX, Part7.LV1
  N13: Part6.RX, Part7.LV2
  N14: Part8.VIN, U3.G$1_S

notes:
  BMP280
